# Fritzing sketch circuit diagram  (saved by Fritzing 0.9.4)
breadboards: 1

parts:
  Part1 = Arduino Uno (Rev3)
  LED1 = smd LED [color="Green (570nm)" package="0603 [SMD]"]
  LED2 = smd LED [color="Red (633nm)" package="0805 [SMD]"]
  M1 = DC Motor
  J1 = Piezo Speaker
  HC-SR04_Sensor_1 = HC-SR04 Ultrasonic Distance Sensor
  M2 = DC Motor
  IC1 = L293D [package=THT]
  VCC1 = Battery block 9V
  VCC2 = Battery block 9V

nets:
  N1: Part1.D8, IC1.In_4
  N2: Part1.D9_PWM, IC1.In_3
  N3: Part1.D10_PWM/SS, J1.pin2
  N4: Part1.D12/MISO, LED2.anode
  N5: Part1.D13/SCK, LED1.anode
  GND: Part1.GND, LED1.cathode, LED2.cathode, J1.pin1, HC-SR04_Sensor_1.GND, IC1.0V, VCC1.-, VCC2.-
  N6: Part1.D2, HC-SR04_Sensor_1.ECHO
  N7: Part1.D3_PWM, HC-SR04_Sensor_1.TRIG
  N8: Part1.D6_PWM, IC1.In_1
  N9: Part1.D7, IC1.In_2
  5V: Part1.5V, HC-SR04_Sensor_1.VCC, IC1.Enable_1, IC1.Enable_2, IC1.+V
  N10: Part1.VIN, VCC2.+
  N11: M1.pin_1, IC1.Out_4_(_Controlled_by_Enable_2_)
  N12: M1.pin_2, IC1.Out_3_(_Controlled_by_Enable_2_)
  N13: M2.pin_1, IC1.Out_2_(_Controlled_by_Enable_1_)
  N14: M2.pin_2, IC1.Out_1_(_Controlled_by_Enable_1_)
  N15: IC1.+Vmotor, VCC1.+

// code stored in the sketch: circuit diagram.ino
 
#define echoPin 2 // attach pin D2 Arduino to pin Echo of HC-SR04
#define trigPin 3 //attach pin D3 Arduino to pin Trig of HC-SR04
#define REDLED 12
#define GREENLED 13
#define l1 6
#define l2 7
#define r1 8
#define r2 9
#define buzzer 10
long duration; // variable for the duration of sound wave travel
int distance; // variable for the distance measurement

void setup() {
  pinMode(trigPin, OUTPUT);
  pinMode(echoPin, INPUT);
  pinMode(REDLED, OUTPUT);
  pinMode(GREENLED, OUTPUT);
  pinMode(l1,OUTPUT);
  pinMode(l2,OUTPUT);
  pinMode(r1,OUTPUT);
  pinMode(r2,OUTPUT);
  Serial.begin(9600); // // Serial Communication is starting with 9600 of baudrate speed
}
void loop() {
  digitalWrite(l1, HIGH);
  digitalWrite(l2, LOW);
  digitalWrite(r1, HIGH);
  digitalWrite(r2, LOW);
  digitalWrite(GREENLED, HIGH);
  digitalWrite(REDLED, LOW);
  digitalWrite(buzzer, LOW);
  // Clears the trigPin condition
  digitalWrite(trigPin, LOW);
  delayMicroseconds(2);
  // Sets the trigPin HIGH (ACTIVE) for 10 microseconds
  digitalWrite(trigPin, HIGH);
  delayMicroseconds(10);
  digitalWrite(trigPin, LOW);
  // Reads the echoPin, returns the sound wave travel time in microseconds
  duration = pulseIn(echoPin, HIGH);
  // Calculating the distance
  distance = duration * 0.034 / 2; // Speed of sound wave divided by 2 (go and back)
  if(distance<20 && distance>10)
  {
   
    digitalWrite(GREENLED,LOW);
    digitalWrite(buzzer,HIGH);
     digitalWrite(REDLED,HIGH);
      delay(100);
   digitalWrite(buzzer,LOW);
     digitalWrite(REDLED,LOW);
      delay(100);
    
  }
  else if(distance<=10)
  {
      digitalWrite(REDLED,HIGH);
      digitalWrite(GREENLED,LOW);
      digitalWrite(buzzer,HIGH);
      digitalWrite(l1,LOW); 
      digitalWrite(l2,LOW); 
      digitalWrite(r1,LOW); 
      digitalWrite(l2,LOW); 
       
  }
  else
  {
    digitalWrite(l1, HIGH);
  digitalWrite(l2, LOW);
  digitalWrite(r1, HIGH);
  digitalWrite(r2, LOW);
  digitalWrite(GREENLED, HIGH);
  digitalWrite(REDLED, LOW);
  digitalWrite(buzzer, LOW);
  }
   Serial.print("Distance: ");
  Serial.print(distance);
  Serial.println(" cm");
  
  
 
}
